// Logisim project Read_Write_Port.circ as structural Verilog: 1 circuit, main circuit main
module main (
  input  Write_Data,
  input  Clock,
  input  [4:0] Write_Reg,
  input  [31:0] Write_Data_2
);

  wire and_1_out, and_2_out, and_3_out, and_4_out, and_5_out, and_6_out, and_7_out, and_8_out, and_9_out,
       and_10_out, and_11_out, and_12_out, and_13_out, and_14_out, and_15_out, and_16_out, and_17_out,
       and_18_out, and_19_out, and_20_out, and_21_out, and_22_out, and_23_out, and_24_out, and_25_out,
       and_26_out, and_27_out, and_28_out, and_29_out, and_30_out, and_31_out, and_32_out, decoder_1_out0,
       decoder_1_out1, decoder_1_out2, decoder_1_out3, decoder_1_out4, decoder_1_out5, decoder_1_out6,
       decoder_1_out7, decoder_1_out8, decoder_1_out9, decoder_1_out10, decoder_1_out11, decoder_1_out12,
       decoder_1_out13, decoder_1_out14, decoder_1_out15, decoder_1_out16, decoder_1_out17, decoder_1_out18,
       decoder_1_out19, decoder_1_out20, decoder_1_out21, decoder_1_out22, decoder_1_out23, decoder_1_out24,
       decoder_1_out25, decoder_1_out26, decoder_1_out27, decoder_1_out28, decoder_1_out29, decoder_1_out30,
       decoder_1_out31;

  Decoder #(.select(5), .enable("false")) decoder_1 (
    .out0(decoder_1_out0), .out1(decoder_1_out1), .out2(decoder_1_out2), .out3(decoder_1_out3),
    .out4(decoder_1_out4), .out5(decoder_1_out5), .out6(decoder_1_out6), .out7(decoder_1_out7),
    .out8(decoder_1_out8), .out9(decoder_1_out9), .out10(decoder_1_out10), .out11(decoder_1_out11),
    .out12(decoder_1_out12), .out13(decoder_1_out13), .out14(decoder_1_out14), .out15(decoder_1_out15),
    .out16(decoder_1_out16), .out17(decoder_1_out17), .out18(decoder_1_out18), .out19(decoder_1_out19),
    .out20(decoder_1_out20), .out21(decoder_1_out21), .out22(decoder_1_out22), .out23(decoder_1_out23),
    .out24(decoder_1_out24), .out25(decoder_1_out25), .out26(decoder_1_out26), .out27(decoder_1_out27),
    .out28(decoder_1_out28), .out29(decoder_1_out29), .out30(decoder_1_out30), .out31(decoder_1_out31),
    .sel(Write_Reg));
  and and_1 (and_1_out, decoder_1_out0, Write_Data);
  and and_2 (and_2_out, decoder_1_out1, Write_Data);
  and and_3 (and_3_out, decoder_1_out2, Write_Data);
  and and_4 (and_4_out, decoder_1_out3, Write_Data);
  and and_5 (and_5_out, decoder_1_out4, Write_Data);
  and and_6 (and_6_out, decoder_1_out5, Write_Data);
  and and_7 (and_7_out, decoder_1_out6, Write_Data);
  and and_8 (and_8_out, decoder_1_out7, Write_Data);
  and and_9 (and_9_out, decoder_1_out8, Write_Data);
  and and_10 (and_10_out, decoder_1_out9, Write_Data);
  and and_11 (and_11_out, decoder_1_out10, Write_Data);
  and and_12 (and_12_out, decoder_1_out11, Write_Data);
  and and_13 (and_13_out, decoder_1_out12, Write_Data);
  and and_14 (and_14_out, decoder_1_out13, Write_Data);
  and and_15 (and_15_out, decoder_1_out14, Write_Data);
  and and_16 (and_16_out, decoder_1_out15, Write_Data);
  and and_17 (and_17_out, decoder_1_out16, Write_Data);
  and and_18 (and_18_out, decoder_1_out17, Write_Data);
  and and_19 (and_19_out, decoder_1_out18, Write_Data);
  and and_20 (and_20_out, decoder_1_out19, Write_Data);
  and and_21 (and_21_out, decoder_1_out20, Write_Data);
  and and_22 (and_22_out, decoder_1_out21, Write_Data);
  and and_23 (and_23_out, decoder_1_out22, Write_Data);
  and and_24 (and_24_out, decoder_1_out23, Write_Data);
  and and_25 (and_25_out, decoder_1_out24, Write_Data);
  and and_26 (and_26_out, decoder_1_out25, Write_Data);
  and and_27 (and_27_out, decoder_1_out26, Write_Data);
  and and_28 (and_28_out, decoder_1_out27, Write_Data);
  and and_29 (and_29_out, decoder_1_out28, Write_Data);
  and and_30 (and_30_out, decoder_1_out29, Write_Data);
  and and_31 (and_31_out, decoder_1_out30, Write_Data);
  and and_32 (and_32_out, decoder_1_out31, Write_Data);
  Register #(.width(32)) r0 (.D(Write_Data_2), .en(and_1_out), .clk(Clock));  // open: Q, clr
  Register #(.width(32)) r1 (.D(Write_Data_2), .en(and_2_out), .clk(Clock));  // open: Q, clr
  Register #(.width(32)) r2 (.D(Write_Data_2), .en(and_3_out), .clk(Clock));  // open: Q, clr
  Register #(.width(32)) r3 (.D(Write_Data_2), .en(and_4_out), .clk(Clock));  // open: Q, clr
  Register #(.width(32)) r4 (.D(Write_Data_2), .en(and_5_out), .clk(Clock));  // open: Q, clr
  Register #(.width(32)) r5 (.D(Write_Data_2), .en(and_6_out), .clk(Clock));  // open: Q, clr
  Register #(.width(32)) r6 (.D(Write_Data_2), .en(and_7_out), .clk(Clock));  // open: Q, clr
  Register #(.width(32)) r7 (.D(Write_Data_2), .en(and_8_out), .clk(Clock));  // open: Q, clr
  Register #(.width(32)) r8 (.D(Write_Data_2), .en(and_9_out), .clk(Clock));  // open: Q, clr
  Register #(.width(32)) r9 (.D(Write_Data_2), .en(and_10_out), .clk(Clock));  // open: Q, clr
  Register #(.width(32)) r10 (.D(Write_Data_2), .en(and_11_out), .clk(Clock));  // open: Q, clr
  Register #(.width(32)) r11 (.D(Write_Data_2), .en(and_12_out), .clk(Clock));  // open: Q, clr
  Register #(.width(32)) r12 (.D(Write_Data_2), .en(and_13_out), .clk(Clock));  // open: Q, clr
  Register #(.width(32)) r13 (.D(Write_Data_2), .en(and_14_out), .clk(Clock));  // open: Q, clr
  Register #(.width(32)) r14 (.D(Write_Data_2), .en(and_15_out), .clk(Clock));  // open: Q, clr
  Register #(.width(32)) r15 (.D(Write_Data_2), .en(and_16_out), .clk(Clock));  // open: Q, clr
  Register #(.width(32)) r16 (.D(Write_Data_2), .en(and_17_out), .clk(Clock));  // open: Q, clr
  Register #(.width(32)) r17 (.D(Write_Data_2), .en(and_18_out), .clk(Clock));  // open: Q, clr
  Register #(.width(32)) r18 (.D(Write_Data_2), .en(and_19_out), .clk(Clock));  // open: Q, clr
  Register #(.width(32)) r19 (.D(Write_Data_2), .en(and_20_out), .clk(Clock));  // open: Q, clr
  Register #(.width(32)) r20 (.D(Write_Data_2), .en(and_21_out), .clk(Clock));  // open: Q, clr
  Register #(.width(32)) r21 (.D(Write_Data_2), .en(and_22_out), .clk(Clock));  // open: Q, clr
  Register #(.width(32)) r22 (.D(Write_Data_2), .en(and_23_out), .clk(Clock));  // open: Q, clr
  Register #(.width(32)) r23 (.D(Write_Data_2), .en(and_24_out), .clk(Clock));  // open: Q, clr
  Register #(.width(32)) r24 (.D(Write_Data_2), .en(and_25_out), .clk(Clock));  // open: Q, clr
  Register #(.width(32)) r25 (.D(Write_Data_2), .en(and_26_out), .clk(Clock));  // open: Q, clr
  Register #(.width(32)) r26 (.D(Write_Data_2), .en(and_27_out), .clk(Clock));  // open: Q, clr
  Register #(.width(32)) r27 (.D(Write_Data_2), .en(and_28_out), .clk(Clock));  // open: Q, clr
  Register #(.width(32)) r28 (.D(Write_Data_2), .en(and_29_out), .clk(Clock));  // open: Q, clr
  Register #(.width(32)) r29 (.D(Write_Data_2), .en(and_30_out), .clk(Clock));  // open: Q, clr
  Register #(.width(32)) r30 (.D(Write_Data_2), .en(and_31_out), .clk(Clock));  // open: Q, clr
  Register #(.width(32)) r31 (.D(Write_Data_2), .en(and_32_out), .clk(Clock));  // open: Q, clr
endmodule
